// Logisim project bla.circ as structural Verilog: 1 circuit, main circuit main
module main (
  input  in_1,
  input  in_2,
  input  in_3,
  output out_4,
  output out_5,
  output out_6,
  output out_7,
  output out_8,
  output out_9,
  output out_10
);

  wire and_1_out, and_2_out, and_4_out, and_5_out, and_6_out, or_2_out;

  and and_1 (and_1_out, in_1, in_3);
  and and_2 (and_2_out, in_3, in_2);
  and and_3 (out_5, in_2, in_1);
  and and_4 (and_4_out, in_3, in_1);
  and and_5 (and_5_out, in_2, in_1);
  and and_6 (and_6_out, in_3, in_2);
  or or_1 (out_6, in_3, and_2_out, and_4_out);
  or or_2 (or_2_out, in_1, and_1_out, and_5_out);
  or or_3 (out_4, in_2, and_6_out, in_1, out_5);

  assign out_9 = out_5;
  assign out_10 = out_4;
endmodule
